// Logisim project step2.circ as structural Verilog: 1 circuit, main circuit main
module main (
  input  x1,
  input  y1,
  input  x2,
  input  y2,
  output f0,
  output f1,
  output f2
);

  wire AND_IC_p3, AND_IC_p6, AND_IC_p10, AND_IC_p12, EXOR_IC_p3, EXOR_IC_p6, EXOR_IC_p9, EXOR_IC_p12;

  // DIP_7486 EXOR_IC: pin names not known; wires that end beside it: x1, 1'b1, EXOR_IC_p3, 1'b1, x2, EXOR_IC_p6, EXOR_IC_p3, y1, EXOR_IC_p9, EXOR_IC_p6, y2, EXOR_IC_p12
  // DIP_7408 AND_IC: pin names not known; wires that end beside it: EXOR_IC_p3, y1, AND_IC_p3, EXOR_IC_p6, y2, AND_IC_p6, EXOR_IC_p9, EXOR_IC_p12, f1, AND_IC_p10, AND_IC_p6, AND_IC_p12
  // DIP_7432 OR_IC: pin names not known; wires that end beside it: EXOR_IC_p3, y1, AND_IC_p10, AND_IC_p12, AND_IC_p3, f0
  // DIP_7402 NOR_IC: pin names not known; wires that end beside it: f2, f1, f0, x1, y1, x2, y2, EXOR_IC_p3, EXOR_IC_p6
endmodule
