// Logisim project step1.circ as structural Verilog: 1 circuit, main circuit main
module main (
  input  A0,
  input  B0,
  input  A1,
  input  B1,
  input  Cin,
  output S1,
  output S0,
  output Cout
);

  wire AND_GATE_p3, AND_GATE_p4, AND_GATE_p6, AND_GATE_p9, AND_GATE_p10, AND_GATE_p11, AND_GATE_p12;

  // DIP_7408 AND_GATE: pin names not known; wires that end beside it: A0, B0, AND_GATE_p3, AND_GATE_p4, Cin, AND_GATE_p6, A1, B1, AND_GATE_p9, AND_GATE_p10, AND_GATE_p11, AND_GATE_p12
  // DIP_7432 OR_GATE: pin names not known; wires that end beside it: AND_GATE_p6, AND_GATE_p3, AND_GATE_p11, AND_GATE_p9, AND_GATE_p12, Cout
  // DIP_7486 EXOR_GATE: pin names not known; wires that end beside it: A0, B0, AND_GATE_p4, AND_GATE_p4, Cin, S0, A1, B1, AND_GATE_p10, AND_GATE_p10, AND_GATE_p11, S1, A0, B0, A1, B1, Cin
endmodule
