// Logisim project step2.circ as structural Verilog: 1 circuit, main circuit main
module main (
  input  A0,
  input  A1,
  input  A2,
  input  A3,
  input  B0,
  input  B1,
  input  B2,
  input  B3,
  input  T_prime_C,
  output S0,
  output S1,
  output S2,
  output S3,
  output C4
);

  wire EXOR_GATE_p3, EXOR_GATE_p6, EXOR_GATE_p9, EXOR_GATE_p12;

  // DIP_7486 EXOR_GATE: pin names not known; wires that end beside it: B0, T_prime_C, EXOR_GATE_p3, B1, T_prime_C, EXOR_GATE_p6, B2, T_prime_C, EXOR_GATE_p9, B3, T_prime_C, EXOR_GATE_p12
  // DIP_74283 _4_BIT_PARALEL_TOPLAYICI_TUMDEVRE: pin names not known; wires that end beside it: S1, A1, EXOR_GATE_p6, S0, A0, EXOR_GATE_p3, T_prime_C, EXOR_GATE_p9, A2, S2, EXOR_GATE_p12, A3, S3, C4, A0, A1, A2, A3, B0, B1, B2, B3, T_prime_C
endmodule
