// Logisim project step3.circ as structural Verilog: 1 circuit, main circuit main
module main (
  input  A3,
  input  A2,
  input  A1,
  input  A0,
  input  B3,
  input  B2,
  input  B1,
  input  B0,
  output A_B,
  output A_B_2,
  output A_B_3
);

  // DIP_7485 _4_BIT_KARSILASTIRICI_TUMDEVRE: pin names not known; wires that end beside it: B3, 1'b1, 1'b1, 1'b1, A_B, A_B_2, A_B_3, A3, B2, A2, A1, B1, A0, B0, A3, A2, A1, A0, B3, B2, B1, B0, 1'b1
endmodule
