// Logisim project exp2.circ as structural Verilog: 1 circuit, main circuit main
module main (
  output QD,
  output QC,
  output QB,
  output QA
);

  wire clock_1_out, dip_7408_1_p3;

  Clock clock_1 (.out(clock_1_out));
  _7493_new u_7493_new_1 (
    .CLK0(clock_1_out), .CLK1(QA), .CLR1(dip_7408_1_p3), .CLR2(dip_7408_1_p3), .Q1(QA), .Q2(QB), .Q3(QC),
    .Q4(QD));
  // DIP_7408 dip_7408_1: pin names not known; wires that end beside it: QB, QD, dip_7408_1_p3
endmodule
