// Logisim project exp3.circ as structural Verilog: 1 circuit, main circuit main
module main (
  output QD,
  output QC,
  output QB,
  output QA
);

  wire clock_1_out, dip_7408_1_p6, dip_7408_1_p9, dip_7476_1_p6;

  Clock clock_1 (.out(clock_1_out));
  // DIP_7476 dip_7476_1: pin names not known; wires that end beside it: clock_1_out, 1'b1, clock_1_out, 1'b1, QA, dip_7476_1_p6, QB, dip_7476_1_p6
  // DIP_7408 dip_7408_1: pin names not known; wires that end beside it: QA, 1'b1, dip_7476_1_p6, dip_7476_1_p6, QB, dip_7408_1_p6, dip_7408_1_p6, QC, dip_7408_1_p9
  // DIP_7476 dip_7476_2: pin names not known; wires that end beside it: clock_1_out, dip_7408_1_p6, clock_1_out, dip_7408_1_p6, QC, dip_7408_1_p9, QD, dip_7408_1_p9
endmodule
