// Logisim project exp4b.circ as structural Verilog: 1 circuit, main circuit main
module main (
  output QA,
  output QB,
  output QC,
  output QD
);

  wire clock_1_out, dip_7400_1_p1, dip_7400_1_p3;

  // DIP_7400 dip_7400_1: pin names not known; wires that end beside it: dip_7400_1_p1, dip_7400_1_p1, dip_7400_1_p3
  Clock clock_1 (.out(clock_1_out));
  // DIP_74161 dip_74161_1: pin names not known; wires that end beside it: clock_1_out, 1'b0, 1'b0, 1'b0, 1'b1, 1'b1, dip_7400_1_p1, QA, QB, QC, QD, 1'b1, dip_7400_1_p3
endmodule
