// Logisim project step1.circ as structural Verilog: 1 circuit, main circuit main
// OR
module main (
  input  x0,
  input  x1,
  input  x2,
  input  x3,
  output g1,
  output g2,
  output g3,
  output g4,
  output g5,
  output g6,
  output g7,
  output g8
);

  // DIP_7408 AND: pin names not known; wires that end beside it: x2, x3, g3, g6, g7, g8, g1, g2, g4, g2, g3
  // DIP_7432 OR: pin names not known; wires that end beside it: x0, x1, g1, g5
  // DIP_7400 NAND: pin names not known; wires that end beside it: x1, x2, g2, x0, g4, g6, x3, g5, g7
endmodule
