// Logisim project step1.circ as structural Verilog: 1 circuit, main circuit main
module main (
  input  x3,
  input  x2,
  input  x1,
  input  x0,
  output f8,
  output f4,
  output f_2,
  output f_1
);

  wire AND_gate_p3, AND_gate_p6, AND_gate_p9, AND_gate_p12, EXOR_gate_p1, EXOR_gate_p4, EXOR_gate_p7,
       EXOR_gate_p13;

  // DIP_7486 EXOR_gate: pin names not known; wires that end beside it: EXOR_gate_p1, 1'b1, x1, EXOR_gate_p4, 1'b1, x2, EXOR_gate_p7, x0, x1, f_2, EXOR_gate_p1, 1'b1, EXOR_gate_p13
  // DIP_7408 AND_gate: pin names not known; wires that end beside it: EXOR_gate_p4, x3, AND_gate_p3, EXOR_gate_p13, x2, AND_gate_p6, x2, EXOR_gate_p1, AND_gate_p9, EXOR_gate_p1, EXOR_gate_p7, AND_gate_p12
  // DIP_7432 OR_gate: pin names not known; wires that end beside it: x0, x1, EXOR_gate_p1, AND_gate_p3, AND_gate_p9, f8, AND_gate_p6, AND_gate_p12, f4, x3, x2, x1, x0

  assign f_1 = x0;
endmodule
