// Logisim project step2.circ as structural Verilog: 1 circuit, main circuit main
module main (
  input  x7,
  input  x6,
  input  x5,
  input  x4,
  input  x3,
  input  x2,
  input  x1,
  input  x0,
  output Z2,
  output Z1,
  output Z0
);

  wire OR_gate1_p4, OR_gate1_p7, OR_gate1_p10, OR_gate1_p13, OR_gate2_p3;

  // DIP_7432 OR_gate1: pin names not known; wires that end beside it: x0, x7, x6, OR_gate1_p4, x5, x4, OR_gate1_p7, x3, x2, OR_gate1_p10, x3, x1, OR_gate1_p13
  // DIP_7432 OR_gate2: pin names not known; wires that end beside it: x7, x5, OR_gate2_p3, OR_gate1_p4, OR_gate1_p7, Z2, OR_gate1_p4, OR_gate1_p10, Z1, OR_gate1_p13, OR_gate2_p3, Z0, x6, x5, x4, x3, x2, x1
endmodule
