// Logisim project 74148_edited2021.circ as structural Verilog: 1 circuit, main circuit 74148_edited
module _74148_edited (
  input  _1__I4,
  input  _16__Vcc,
  input  _2__I5,
  input  _15__nEO__NC,
  input  _3__I6,
  input  _14__nGS__NC,
  input  _4__I7,
  input  _13__I3,
  input  _5__nEI__NC,
  input  _12__I2,
  input  _11__I1,
  input  _10__I0,
  input  _8__GND,
  output _6__A2,
  output _7__A1,
  output _9__A0
);

  wire a_0, a_1, a_2, not_1_out, not_2_out, not_3_out, not_4_out, not_7_out, not_8_out, not_9_out;
  wire [2:0] priority_encoder_1_out;

  not not_1 (not_1_out, _1__I4);
  not not_2 (not_2_out, _2__I5);
  not not_3 (not_3_out, _3__I6);
  not not_4 (not_4_out, _4__I7);
  not not_5 (a_2, priority_encoder_1_out[2]);
  not not_6 (a_1, priority_encoder_1_out[1]);
  Priority_Encoder priority_encoder_1 (
    .in0(1'b1), .in1(not_9_out), .in2(not_8_out), .in3(not_7_out), .in4(not_1_out), .in5(not_2_out),
    .in6(not_3_out), .in7(not_4_out), .out(priority_encoder_1_out));  // open: en_in, gs, en_out
  not not_7 (not_7_out, _13__I3);
  not not_8 (not_8_out, _12__I2);
  not not_9 (not_9_out, _11__I1);
  not not_10 (a_0, priority_encoder_1_out[0]);
  or or_1 (_6__A2, _5__nEI__NC, a_2);
  or or_2 (_7__A1, _5__nEI__NC, a_1);
  or or_3 (_9__A0, _5__nEI__NC, a_0);

  // Other names for the same wires on the sheet: a_0_o = _9__A0; a_1_o = _7__A1; a_2_o = _6__A2; en_o = _5__nEI__NC

  // Notes on the sheet:
  //   74148:Active_low 9-Line to 4-Line Priority Encoder
  //   NOTE: Pins 5, 14, and 15 have connections normally, but I chose not to model them
endmodule
