// Logisim project 7493_edited.circ as structural Verilog: 1 circuit, main circuit 7493_new
module _7493_new (
  input  CLK0,
  input  CLK1,
  input  CLR1,
  input  CLR2,
  output Q1,
  output Q2,
  output Q3,
  output Q4
);

  wire and_1_out, d_flip_flop_1_p1, d_flip_flop_2_p1, d_flip_flop_3_p1, d_flip_flop_4_p1, not_1_out,
       not_2_out, not_3_out, not_4_out;

  not not_1 (not_1_out, CLK0);
  not not_2 (not_2_out, CLK1);
  and and_1 (and_1_out, CLR1, CLR2);
  not not_3 (not_3_out, Q2);
  not not_4 (not_4_out, Q3);
  // D_Flip_Flop d_flip_flop_1: pin names not known; wires that end beside it: d_flip_flop_1_p1, not_1_out, and_1_out, Q1, d_flip_flop_1_p1
  // D_Flip_Flop d_flip_flop_2: pin names not known; wires that end beside it: d_flip_flop_2_p1, not_2_out, and_1_out, Q2, d_flip_flop_2_p1
  // D_Flip_Flop d_flip_flop_3: pin names not known; wires that end beside it: d_flip_flop_3_p1, not_3_out, and_1_out, Q3, d_flip_flop_3_p1
  // D_Flip_Flop d_flip_flop_4: pin names not known; wires that end beside it: d_flip_flop_4_p1, not_4_out, and_1_out, Q4, d_flip_flop_4_p1
endmodule
