// Logisim project step1.circ as structural Verilog: 1 circuit, main circuit main
module main (
  input  x0,
  input  x1,
  input  x2,
  output f1,
  output f2
);

  wire AND_GATE_p3, AND_GATE_p6, KOD_COZUCU_TUMDEVRE_p7, KOD_COZUCU_TUMDEVRE_p8, KOD_COZUCU_TUMDEVRE_p9,
       KOD_COZUCU_TUMDEVRE_p10, KOD_COZUCU_TUMDEVRE_p11;

  // DIP_74138 KOD_COZUCU_TUMDEVRE: pin names not known; wires that end beside it: x0, x1, x2, 1'b0, 1'b0, 1'b1, KOD_COZUCU_TUMDEVRE_p7, KOD_COZUCU_TUMDEVRE_p8, KOD_COZUCU_TUMDEVRE_p9, KOD_COZUCU_TUMDEVRE_p10, KOD_COZUCU_TUMDEVRE_p11
  // DIP_7408 AND_GATE: pin names not known; wires that end beside it: KOD_COZUCU_TUMDEVRE_p7, KOD_COZUCU_TUMDEVRE_p8, AND_GATE_p3, KOD_COZUCU_TUMDEVRE_p9, KOD_COZUCU_TUMDEVRE_p10, AND_GATE_p6, AND_GATE_p3, KOD_COZUCU_TUMDEVRE_p11, f1, AND_GATE_p3, AND_GATE_p6, f2
endmodule
