// Logisim project step2.circ as structural Verilog: 1 circuit, main circuit main
module main (
  input  x0,
  input  x1,
  input  x2,
  output f1,
  output f2
);

  wire NOT_GATE_p2;

  // DIP_7404 NOT_GATE: pin names not known; wires that end beside it: x0, NOT_GATE_p2
  // DIP_74153 MULTIPLEXER: pin names not known; wires that end beside it: 1'b0, x2, x0, 1'b1, NOT_GATE_p2, x0, f1, 1'b0, x1, 1'b1, 1'b0, NOT_GATE_p2, x0, f2
endmodule
