// Logisim project step3.circ as structural Verilog: 1 circuit, main circuit main
module main (
  input  x0,
  input  x1,
  input  x2,
  output f1,
  output f2,
  output f3
);

  wire _3_8_Decoder_p7, _3_8_Decoder_p8, _3_8_Decoder_p9, _3_8_Decoder_p10, _3_8_Decoder_p11,
       _3_8_Decoder_p12, _3_8_Decoder_p13, _3_8_Decoder_p14;

  // DIP_74138 _3_8_Decoder: pin names not known; wires that end beside it: x0, x1, x2, 1'b0, 1'b0, 1'b1, _3_8_Decoder_p7, _3_8_Decoder_p8, _3_8_Decoder_p9, _3_8_Decoder_p10, _3_8_Decoder_p11, _3_8_Decoder_p12, _3_8_Decoder_p13, _3_8_Decoder_p14
  _74148_edited _8_3_Encoder (
    ._1__I4(_3_8_Decoder_p9), ._2__I5(_3_8_Decoder_p8), ._3__I6(_3_8_Decoder_p7), ._4__I7(_3_8_Decoder_p14),
    ._5__nEI__NC(1'b0), ._7__A1(f2), ._8__GND(1'b0), ._16__Vcc(1'b1), ._13__I3(_3_8_Decoder_p10),
    ._12__I2(_3_8_Decoder_p11), ._11__I1(_3_8_Decoder_p12), ._10__I0(_3_8_Decoder_p13), ._9__A0(f3),
    ._6__A2(f1));  // open: _15__nEO__NC, _14__nGS__NC
endmodule
