// Logisim project step1.circ as structural Verilog: 1 circuit, main circuit main
module main (
  input  Clear1,
  input  x,
  input  Set1,
  input  Clear2,
  input  Set2,
  output q1,
  output q2,
  output z
);

  wire Clock_out, dip_7400_1_p1, dip_7400_1_p4, dip_7400_1_p6, dip_7400_1_p7, dip_7400_1_p12, dip_7474_1_p2,
       dip_7486_1_p3, dip_7486_1_p5;

  Clock Clock (.out(Clock_out));
  // DIP_7486 dip_7486_1: pin names not known; wires that end beside it: x, 1'b1, dip_7486_1_p3, x, dip_7486_1_p5, x, dip_7486_1_p5, z, q2
  // DIP_7400 dip_7400_1: pin names not known; wires that end beside it: dip_7400_1_p1, dip_7486_1_p3, q2, dip_7400_1_p4, dip_7400_1_p4, dip_7400_1_p6, dip_7400_1_p7, q1, dip_7400_1_p6, q1, dip_7486_1_p5, dip_7400_1_p12, dip_7400_1_p12, dip_7400_1_p1
  // DIP_7474 dip_7474_1: pin names not known; wires that end beside it: Clear1, dip_7474_1_p2, Clock_out, Set1, q1, dip_7474_1_p2, Clear2, Set2, dip_7400_1_p7, Clock_out, q2, dip_7486_1_p5
endmodule
