// Logisim project step1.circ as structural Verilog: 1 circuit, main circuit main
module main (
  input  X,
  input  CLR3,
  input  PRS3,
  input  CLR2,
  input  PR2,
  input  CLR1,
  input  PRS1,
  output Q1,
  output Q2,
  output Q3,
  output Z
);

  wire JK_p1, NAND_2_p2, NAND_2_p6, NAND_2_p9, NAND_p3, NAND_p5, NAND_p6, NAND_p8, NAND_p9;

  // DIP_7400 NAND: pin names not known; wires that end beside it: X, Q2, NAND_p3, NAND_p3, NAND_p5, NAND_p6, Q3, NAND_p8, NAND_p9
  // DIP_7400 NAND_2: pin names not known; wires that end beside it: X, NAND_2_p2, NAND_p5, X, X, NAND_2_p6, Q2, NAND_2_p6, NAND_2_p9, NAND_p9, NAND_p9, Z
  // DIP_7476 JK: pin names not known; wires that end beside it: JK_p1, PRS1, CLR1, Q2, NAND_p8, Q1, NAND_2_p2
  // DIP_7476 JK_2: pin names not known; wires that end beside it: JK_p1, PR2, CLR2, NAND_2_p2, JK_p1, PRS3, CLR3, Q1, Q2, NAND_p8, NAND_2_p9, Q3, NAND_p6
  Clock clock_1 (.out(JK_p1));
endmodule
