// Logisim project exp1.circ as structural Verilog: 1 circuit, main circuit main
module main (
  output QD,
  output QC,
  output QB,
  output QA
);

  wire clock_1_out;

  Clock clock_1 (.out(clock_1_out));
  // DIP_7476 dip_7476_1: pin names not known; wires that end beside it: clock_1_out, 1'b1, QA, 1'b1, QA, 1'b1, QB, 1'b1
  // DIP_7476 dip_7476_2: pin names not known; wires that end beside it: QB, 1'b1, QC, 1'b1, QC, 1'b1, QD, 1'b1
endmodule
